// Logisim project MIPS32.circ as structural Verilog
module Registers (
  input  CLK,
  input  [4:0] ReadRegister1,
  input  [4:0] ReadRegister2,
  input  [4:0] WriteRegister,
  input  [31:0] WriteData,
  input  Write,
  input  [31:0] PC,
  input  WCLK,
  output [31:0] ReadData1,
  output [31:0] ReadData2
);

  wire decoder_1_out0, decoder_1_out1, decoder_1_out2, decoder_1_out3, decoder_1_out4, decoder_1_out5,
       decoder_1_out6, decoder_1_out7, decoder_1_out8, decoder_1_out9, decoder_1_out10, decoder_1_out11,
       decoder_1_out12, decoder_1_out13, decoder_1_out14, decoder_1_out15, decoder_1_out16, decoder_1_out17,
       decoder_1_out18, decoder_1_out19, decoder_1_out20, decoder_1_out21, decoder_1_out22, decoder_1_out23,
       decoder_1_out24, decoder_1_out25, decoder_1_out26, decoder_1_out27, decoder_1_out28, decoder_1_out29,
       decoder_1_out30, decoder_1_out31, multiplexer_1_out, not_1_out, selclk, undriven;
  wire [31:0] multiplexer_2_out, register_1_q, register_2_q, register_3_q, register_4_q, register_5_q,
       register_6_q, register_7_q, register_8_q, register_9_q, register_10_q, register_11_q, register_12_q,
       register_13_q, register_14_q, register_15_q, register_16_q, register_17_q, register_18_q,
       register_19_q, register_20_q, register_21_q, register_22_q, register_23_q, register_24_q,
       register_25_q, register_26_q, register_27_q, register_28_q, register_29_q, register_30_q,
       register_31_q, register_32_q;

  Decoder #(.select(5)) decoder_1 (
    .out0(decoder_1_out0), .out1(decoder_1_out1), .out2(decoder_1_out2), .out3(decoder_1_out3),
    .out4(decoder_1_out4), .out5(decoder_1_out5), .out6(decoder_1_out6), .out7(decoder_1_out7),
    .out8(decoder_1_out8), .out9(decoder_1_out9), .out10(decoder_1_out10), .out11(decoder_1_out11),
    .out12(decoder_1_out12), .out13(decoder_1_out13), .out14(decoder_1_out14), .out15(decoder_1_out15),
    .out16(decoder_1_out16), .out17(decoder_1_out17), .out18(decoder_1_out18), .out19(decoder_1_out19),
    .out20(decoder_1_out20), .out21(decoder_1_out21), .out22(decoder_1_out22), .out23(decoder_1_out23),
    .out24(decoder_1_out24), .out25(decoder_1_out25), .out26(decoder_1_out26), .out27(decoder_1_out27),
    .out28(decoder_1_out28), .out29(decoder_1_out29), .out30(decoder_1_out30), .out31(decoder_1_out31),
    .sel(WriteRegister), .en(selclk));
  not not_1 (not_1_out, CLK);
  and and_1 (selclk, not_1_out, Write);
  Multiplexer multiplexer_1 (.in0(CLK), .in1(WCLK), .out(multiplexer_1_out), .sel(selclk));
  Multiplexer #(.width(32)) multiplexer_2 (.in0(WriteData), .in1(PC), .out(multiplexer_2_out), .sel(undriven));
  Register #(.width(32)) register_1 (
    .D(WriteData), .en(decoder_1_out0), .clk(multiplexer_1_out), .Q(register_1_q));  // open: clr
  Register #(.width(32)) register_2 (
    .D(WriteData), .en(decoder_1_out1), .clk(multiplexer_1_out), .Q(register_2_q));  // open: clr
  Register #(.width(32)) register_3 (
    .D(WriteData), .en(decoder_1_out2), .clk(multiplexer_1_out), .Q(register_3_q));  // open: clr
  Register #(.width(32)) register_4 (
    .D(WriteData), .en(decoder_1_out3), .clk(multiplexer_1_out), .Q(register_4_q));  // open: clr
  Register #(.width(32)) register_5 (
    .D(WriteData), .en(decoder_1_out4), .clk(multiplexer_1_out), .Q(register_5_q));  // open: clr
  Register #(.width(32)) register_6 (
    .D(WriteData), .en(decoder_1_out5), .clk(multiplexer_1_out), .Q(register_6_q));  // open: clr
  Register #(.width(32)) register_7 (
    .D(WriteData), .en(decoder_1_out6), .clk(multiplexer_1_out), .Q(register_7_q));  // open: clr
  Register #(.width(32)) register_8 (
    .D(WriteData), .en(decoder_1_out7), .clk(multiplexer_1_out), .Q(register_8_q));  // open: clr
  Register #(.width(32)) register_9 (
    .D(WriteData), .en(decoder_1_out8), .clk(multiplexer_1_out), .Q(register_9_q));  // open: clr
  Register #(.width(32)) register_10 (
    .D(WriteData), .en(decoder_1_out9), .clk(multiplexer_1_out), .Q(register_10_q));  // open: clr
  Register #(.width(32)) register_11 (
    .D(WriteData), .en(decoder_1_out10), .clk(multiplexer_1_out), .Q(register_11_q));  // open: clr
  Register #(.width(32)) register_12 (
    .D(WriteData), .en(decoder_1_out11), .clk(multiplexer_1_out), .Q(register_12_q));  // open: clr
  Register #(.width(32)) register_13 (
    .D(WriteData), .en(decoder_1_out12), .clk(multiplexer_1_out), .Q(register_13_q));  // open: clr
  Register #(.width(32)) register_14 (
    .D(WriteData), .en(decoder_1_out13), .clk(multiplexer_1_out), .Q(register_14_q));  // open: clr
  Register #(.width(32)) register_15 (
    .D(WriteData), .en(decoder_1_out14), .clk(multiplexer_1_out), .Q(register_15_q));  // open: clr
  Register #(.width(32)) register_16 (
    .D(WriteData), .en(decoder_1_out15), .clk(multiplexer_1_out), .Q(register_16_q));  // open: clr
  Register #(.width(32)) register_17 (
    .D(WriteData), .en(decoder_1_out16), .clk(multiplexer_1_out), .Q(register_17_q));  // open: clr
  Register #(.width(32)) register_18 (
    .D(WriteData), .en(decoder_1_out17), .clk(multiplexer_1_out), .Q(register_18_q));  // open: clr
  Register #(.width(32)) register_19 (
    .D(WriteData), .en(decoder_1_out18), .clk(multiplexer_1_out), .Q(register_19_q));  // open: clr
  Register #(.width(32)) register_20 (
    .D(WriteData), .en(decoder_1_out19), .clk(multiplexer_1_out), .Q(register_20_q));  // open: clr
  Register #(.width(32)) register_21 (
    .D(WriteData), .en(decoder_1_out20), .clk(multiplexer_1_out), .Q(register_21_q));  // open: clr
  Register #(.width(32)) register_22 (
    .D(WriteData), .en(decoder_1_out21), .clk(multiplexer_1_out), .Q(register_22_q));  // open: clr
  Register #(.width(32)) register_23 (
    .D(WriteData), .en(decoder_1_out22), .clk(multiplexer_1_out), .Q(register_23_q));  // open: clr
  Register #(.width(32)) register_24 (
    .D(WriteData), .en(decoder_1_out23), .clk(multiplexer_1_out), .Q(register_24_q));  // open: clr
  Register #(.width(32)) register_25 (
    .D(WriteData), .en(decoder_1_out24), .clk(multiplexer_1_out), .Q(register_25_q));  // open: clr
  Register #(.width(32)) register_26 (
    .D(WriteData), .en(decoder_1_out25), .clk(multiplexer_1_out), .Q(register_26_q));  // open: clr
  Register #(.width(32)) register_27 (
    .D(WriteData), .en(decoder_1_out26), .clk(multiplexer_1_out), .Q(register_27_q));  // open: clr
  Register #(.width(32)) register_28 (
    .D(WriteData), .en(decoder_1_out27), .clk(multiplexer_1_out), .Q(register_28_q));  // open: clr
  Register #(.width(32)) register_29 (
    .D(WriteData), .en(decoder_1_out28), .clk(multiplexer_1_out), .Q(register_29_q));  // open: clr
  Register #(.width(32)) register_30 (
    .D(WriteData), .en(decoder_1_out29), .clk(multiplexer_1_out), .Q(register_30_q));  // open: clr
  Register #(.width(32)) register_31 (
    .D(WriteData), .en(decoder_1_out30), .clk(multiplexer_1_out), .Q(register_31_q));  // open: clr
  Register #(.width(32)) register_32 (
    .D(multiplexer_2_out), .en(decoder_1_out31), .clk(multiplexer_1_out), .Q(register_32_q));  // open: clr
  Multiplexer #(.select(5), .width(32)) multiplexer_3 (
    .in0(register_1_q), .in1(register_2_q), .in2(register_3_q), .in3(register_4_q), .in4(register_5_q),
    .in5(register_6_q), .in6(register_7_q), .in7(register_8_q), .in8(register_9_q), .in9(register_10_q),
    .in10(register_11_q), .in11(register_12_q), .in12(register_13_q), .in13(register_14_q),
    .in14(register_15_q), .in15(register_16_q), .in16(register_17_q), .in17(register_18_q),
    .in18(register_19_q), .in19(register_20_q), .in20(register_21_q), .in21(register_22_q),
    .in22(register_23_q), .in23(register_24_q), .in24(register_25_q), .in25(register_26_q),
    .in26(register_27_q), .in27(register_28_q), .in28(register_29_q), .in29(register_30_q),
    .in30(register_31_q), .in31(register_32_q), .out(ReadData1), .sel(ReadRegister1));
  Multiplexer #(.select(5), .width(32)) multiplexer_4 (
    .in0(register_1_q), .in1(register_2_q), .in2(register_3_q), .in3(register_4_q), .in4(register_5_q),
    .in5(register_6_q), .in6(register_7_q), .in7(register_8_q), .in8(register_9_q), .in9(register_10_q),
    .in10(register_11_q), .in11(register_12_q), .in12(register_13_q), .in13(register_14_q),
    .in14(register_15_q), .in15(register_16_q), .in16(register_17_q), .in17(register_18_q),
    .in18(register_19_q), .in19(register_20_q), .in20(register_21_q), .in21(register_22_q),
    .in22(register_23_q), .in23(register_24_q), .in24(register_25_q), .in25(register_26_q),
    .in26(register_27_q), .in27(register_28_q), .in28(register_29_q), .in29(register_30_q),
    .in30(register_31_q), .in31(register_32_q), .out(ReadData2), .sel(ReadRegister2));

  // Other names for the same wires on the sheet: C = CLK; wcc = WCLK; WD[31:0] = WriteData

  // Notes on the sheet:
  //   na CLK citaj
  //   na wcc i we
endmodule

module ALU (
  input  [31:0] Operand1,
  input  [31:0] Operand2,
  input  [10:0] ALUfunc,
  output ZF,
  output [31:0] Result
);

  wire [31:0] Add, aright, BAnd, bnor, bor, bxor, logleft, logright, lui, multiplexer_1_out,
       multiplexer_2_out, shifter_1_out, slt, sub;

  Shifter #(.width(32)) shifter_1 (.in(Operand2), .\dist (5'b10000), .out(shifter_1_out));
  Shifter shifter_2 ();  // open: in, dist, out
  Shifter #(.width(32)) shifter_3 (.in(Operand1), .\dist (ALUfunc[4:0]), .out(logleft));
  Shifter #(.shift("lr"), .width(32)) shifter_4 (.in(Operand1), .\dist (ALUfunc[4:0]), .out(logright));
  Shifter #(.shift("ar"), .width(32)) shifter_5 (.in(Operand1), .\dist (ALUfunc[4:0]), .out(aright));
  Shifter #(.shift("rl"), .width(32)) shifter_6 (.in(Operand1), .\dist (ALUfunc[4:0]));  // open: out
  Shifter #(.shift("rr"), .width(32)) shifter_7 (.in(Operand1), .\dist (ALUfunc[4:0]));  // open: out
  Adder #(.width(32)) adder_1 (.a(Operand1), .b(Operand2), .out(Add));  // open: cin, cout
  Subtractor #(.width(32)) subtractor_1 (.a(Operand1), .b(Operand2), .out(sub));  // open: bin, bout
  assign BAnd = Operand1 & Operand2;  // AND_Gate and_1, 32 bits wide
  assign bor = Operand1 | Operand2;  // OR_Gate or_1, 32 bits wide
  // NOT_Gate not_1 has open pins: in=Operand1, out=open
  assign bxor = Operand1 ^ Operand2;  // XOR_Gate xor_1, 32 bits wide
  Negator #(.width(32)) negator_1 (.in(Operand1));  // open: out
  sltkolo sltkolo_1 (.operand1(Operand1), .operand2(Operand2), .out_3(slt));
  Adder #(.width(32)) adder_2 (.a(Operand1), .b(shifter_1_out), .out(lui));  // open: cin, cout
  Adder adder_3 ();  // open: a, b, out, cin, cout
  assign bnor = ~bor;  // NOT_Gate not_2, 32 bits wide
  Multiplexer #(.select(5), .width(32)) multiplexer_1 (
    .in0(logleft), .in2(logright), .in3(aright), .in8(Operand1), .in17(lui), .out(multiplexer_1_out),
    .sel(ALUfunc[9:5]));  // open: in1, in4, in5, in6, in7, in9, in10, in11, in12, in13, in14, in15, in16, in18, in19, in20, in21, in22, in23, in24, in25, in26, in27, in28, in29, in30, in31
  Multiplexer #(.select(5), .width(32)) multiplexer_2 (
    .in0(Add), .in2(sub), .in4(BAnd), .in5(bor), .in6(bxor), .in7(bnor), .in10(slt), .out(multiplexer_2_out));  // open: in1, in3, in8, in9, in11, in12, in13, in14, in15, in16, in17, in18, in19, in20, in21, in22, in23, in24, in25, in26, in27, in28, in29, in30, in31, sel
  Multiplexer #(.width(32)) multiplexer_3 (
    .in0(multiplexer_1_out), .in1(multiplexer_2_out), .out(Result), .sel(ALUfunc[10]));
  and and_2 (ZF, ~Result[0], ~Result[1], ~Result[2], ~Result[3], ~Result[4], ~Result[5], ~Result[6], ~Result[7], ~Result[8], ~Result[9], ~Result[10], ~Result[11], ~Result[12], ~Result[13], ~Result[14], ~Result[15], ~Result[17], ~Result[18], ~Result[19], ~Result[20], ~Result[21], ~Result[22], ~Result[23], ~Result[24], ~Result[25], ~Result[26], ~Result[27], ~Result[28], ~Result[29], ~Result[30], ~Result[31], ~Result[16]);  // AND_Gate

  // Other names for the same wires on the sheet: allpass[31:0] = Operand1; LS[4:0] = ALUfunc[9:5]; HS = ALUfunc[10]

  // Notes on the sheet:
  //   velicina?
endmodule

module Data (
  input  CLK,
  input  [31:0] Address,
  input  MemWrite,
  input  MemRead,
  input  [31:0] WriteData,
  input  [1:0] Mode,
  output [31:0] ReadData
);

  wire [7:0] multiplexer_2_out, ram_1_dout, ram_2_dout, ram_3_dout, ram_4_dout;
  wire [15:0] multiplexer_1_out;
  wire [31:0] signextend_1_value_u32, signextendbyte_1_a32;

  RAM ram_1 (.addr(Address[7:0]), .we(MemWrite), .oe(MemRead), .clk(CLK), .din(WriteData[7:0]), .dout(ram_1_dout));
  RAM ram_2 (.addr(Address[15:8]), .we(MemWrite), .oe(MemRead), .clk(CLK), .din(WriteData[15:8]), .dout(ram_2_dout));
  RAM ram_3 (.addr(Address[23:16]), .we(MemWrite), .oe(MemRead), .clk(CLK), .din(WriteData[23:16]), .dout(ram_3_dout));
  RAM ram_4 (.addr(Address[31:24]), .we(MemWrite), .oe(MemRead), .clk(CLK), .din(WriteData[31:24]), .dout(ram_4_dout));
  Multiplexer #(.width(16)) multiplexer_1 (
    .in0({ram_2_dout, ram_1_dout}), .out(multiplexer_1_out), .sel(Address[1]));  // open: in1
  Multiplexer #(.select(2), .width(8)) multiplexer_2 (
    .in0(ram_1_dout), .in1(ram_2_dout), .in2(ram_3_dout), .in3(ram_4_dout), .out(multiplexer_2_out),
    .sel(Address[1:0]));
  SignExtend signextend_1 (.Value_u16(multiplexer_1_out), .Value_u32(signextend_1_value_u32));
  SignExtendByte signextendbyte_1 (.a(multiplexer_2_out), .a32(signextendbyte_1_a32));
  Multiplexer #(.select(2), .width(32)) multiplexer_3 (
    .in0({ram_4_dout, ram_3_dout, ram_2_dout, ram_1_dout}), .in1(signextend_1_value_u32),
    .in2(signextendbyte_1_a32), .out(ReadData), .sel(Mode));  // open: in3
endmodule

module Instructions (
  input  [31:0] Read,
  output [31:0] Instruction
);

  ROM #(.addrWidth(16), .dataWidth(32)) rom_1 (.addr(Read[15:0]), .data(Instruction));
endmodule

module SignExtend (
  input  [15:0] Value_u16,
  output [31:0] Value_u32
);


  assign Value_u32 = {{17{Value_u16[15]}}, Value_u16[14:0]};
endmodule

module Control (
  input  [5:0] Opcode,
  output RegDst,
  output Branch,
  output MemRead,
  output MemToReg,
  output MemWrite,
  output ALUSrc,
  output RegWrite,
  output [1:0] AdrMode,
  output [5:0] ALUop,
  output RegToPC
);

  wire [4:4] rom_1_data;

  ROM #(.addrWidth(6)) rom_1 (
    .addr(Opcode), .data({RegWrite, ALUSrc, MemWrite, rom_1_data[4], MemToReg, MemRead, Branch, RegDst}));
  ROM #(.addrWidth(6), .dataWidth(6)) rom_2 (.addr(Opcode), .data(ALUop));
  ROM #(.addrWidth(6), .dataWidth(2)) rom_3 (.addr(Opcode), .data(AdrMode));

  // Notes on the sheet:
  //   contents of rom_1 (hex, n*v repeats v):
  //   0 0 4*42 0 0 3 0 3 0 3 3 0 1 16*0 33 0 0 33 4*0 6 0 0 6
  //   contents of rom_2 (hex, n*v repeats v):
  //   3f 0 0 0 22 22 0 0 20 0 2a 0 24 25 0 11 16*0 20 0 0 20 4*0 20 0 0 20
  //   contents of rom_3 (hex, n*v repeats v):
  //   32*0 2 7*0 2
endmodule

module ALUControl (
  input  [4:0] SHAMT,
  input  [5:0] ALUop,
  input  [5:0] Func,
  output [10:0] ALUFunc
);

  wire and_1_out;

  Multiplexer #(.width(6)) multiplexer_1 (.in0(ALUop), .in1(Func), .out(ALUFunc[10:5]), .sel(and_1_out));
  and and_1 (and_1_out, ALUop[0], ALUop[1], ALUop[2], ALUop[4], ALUop[5], ALUop[3]);

  assign ALUFunc[4:0] = SHAMT;
endmodule

module sltkolo (
  input  [31:0] operand1,
  input  [31:0] operand2,
  output [31:0] out_3
);

  wire [30:0] subtractor_1_out;

  Subtractor #(.width(32)) subtractor_1 (
    .a(operand1), .b(operand2), .out({out_3[0], subtractor_1_out}));  // open: bin, bout

  assign out_3[31:1] = {31{1'b0}};
endmodule

module CLKmodul (
  input  CLK,
  input  RST,
  output phase0,
  output phase90
);

  wire d_ff_1_qn, d_ff_2_qn, not_1_out;

  D_Flip_Flop d_ff_1 (.D(d_ff_1_qn), .clk(CLK), .Q(phase0), .Qn(d_ff_1_qn), .reset(RST));  // open: preset
  D_Flip_Flop d_ff_2 (.D(d_ff_2_qn), .clk(not_1_out), .Q(phase90), .Qn(d_ff_2_qn), .reset(RST));  // open: preset
  not not_1 (not_1_out, CLK);
endmodule

module IF2ID (
  input  [31:0] PCin,
  input  [31:0] InsIn,
  input  en,
  input  CLK,
  output [31:0] NPC,
  output [31:0] Ins
);

  Register #(.width(32)) NextPC (.D(PCin), .en(en), .clk(CLK), .Q(NPC));  // open: clr
  Register #(.width(32)) Instruction (.D(InsIn), .en(en), .clk(CLK), .Q(Ins));  // open: clr
endmodule

module ID2EX (
  input  flush,
  input  CLK,
  input  [31:0] NPC,
  input  [31:0] InsIn,
  input  [31:0] OP1in,
  input  [31:0] OP2in,
  input  [31:0] SEin,
  input  [4:0] RegDstIn,
  input  [5:0] ALUOPIN,
  input  ALUSrcIN,
  input  RegDstMUXin,
  input  BranchIn,
  input  MemWriteIn,
  input  MemReadIn,
  input  RegWriteIn,
  input  MemToRegIn,
  input  [4:0] rtin,
  input  [4:0] rsin,
  input  [4:0] rdin,
  input  [1:0] AdrMode,
  output [31:0] NextPC,
  output [31:0] Ins,
  output [31:0] OP1out,
  output [31:0] OP2out,
  output [31:0] SEout,
  output [4:0] RegDstOut,
  output [5:0] ALUOPOUT,
  output ALUSrcOut,
  output RegDstMUXout,
  output BranchOut,
  output MemWriteOut,
  output MemReadOut,
  output RegWriteOut,
  output MemToRegOut,
  output [4:0] rtout,
  output [4:0] rsout,
  output [4:0] rdout,
  output [1:0] Mode
);

  wire multiplexer_7_out, multiplexer_8_out, multiplexer_9_out, multiplexer_10_out, multiplexer_11_out,
       multiplexer_12_out, multiplexer_13_out;
  wire [1:0] multiplexer_16_out;
  wire [4:0] multiplexer_5_out, multiplexer_14_out, multiplexer_15_out, multiplexer_18_out;
  wire [5:0] multiplexer_6_out;
  wire [31:0] multiplexer_1_out, multiplexer_2_out, multiplexer_3_out, multiplexer_4_out, multiplexer_17_out;

  Multiplexer #(.width(32)) multiplexer_1 (.in0(NPC), .in1({32{1'b0}}), .out(multiplexer_1_out), .sel(flush));
  Multiplexer #(.width(32)) multiplexer_2 (.in0(InsIn), .in1({32{1'b0}}), .out(multiplexer_2_out), .sel(flush));
  Multiplexer #(.width(32)) multiplexer_3 (.in0(OP1in), .in1({32{1'b0}}), .out(multiplexer_3_out), .sel(flush));
  Multiplexer #(.width(32)) multiplexer_4 (.in0(OP2in), .in1({32{1'b0}}), .out(multiplexer_4_out), .sel(flush));
  Multiplexer #(.width(5)) multiplexer_5 (.in0(RegDstIn), .in1({5{1'b0}}), .out(multiplexer_5_out), .sel(flush));
  Multiplexer #(.width(6)) multiplexer_6 (.in0(ALUOPIN), .in1({6{1'b0}}), .out(multiplexer_6_out), .sel(flush));
  Multiplexer multiplexer_7 (.in0(ALUSrcIN), .in1(1'b0), .out(multiplexer_7_out), .sel(flush));
  Multiplexer multiplexer_8 (.in0(RegDstMUXin), .in1(1'b0), .out(multiplexer_8_out), .sel(flush));
  Multiplexer multiplexer_9 (.in0(BranchIn), .in1(1'b0), .out(multiplexer_9_out), .sel(flush));
  Multiplexer multiplexer_10 (.in0(MemWriteIn), .in1(1'b0), .out(multiplexer_10_out), .sel(flush));
  Multiplexer multiplexer_11 (.in0(MemReadIn), .in1(1'b0), .out(multiplexer_11_out), .sel(flush));
  Multiplexer multiplexer_12 (.in0(RegWriteIn), .in1(1'b0), .out(multiplexer_12_out), .sel(flush));
  Multiplexer multiplexer_13 (.in0(MemToRegIn), .in1(1'b0), .out(multiplexer_13_out), .sel(flush));
  Multiplexer #(.width(5)) multiplexer_14 (.in0(rtin), .in1({5{1'b0}}), .out(multiplexer_14_out), .sel(flush));
  Multiplexer #(.width(5)) multiplexer_15 (.in0(rsin), .in1({5{1'b0}}), .out(multiplexer_15_out), .sel(flush));
  Multiplexer #(.width(2)) multiplexer_16 (.in0(AdrMode), .in1(2'b00), .out(multiplexer_16_out), .sel(flush));
  Multiplexer #(.width(32)) multiplexer_17 (.in0(SEin), .in1({32{1'b0}}), .out(multiplexer_17_out), .sel(flush));
  Multiplexer #(.width(5)) multiplexer_18 (.in0(rdin), .in1({5{1'b0}}), .out(multiplexer_18_out), .sel(flush));
  Register #(.width(32)) register_1 (.D(multiplexer_1_out), .en(1'b1), .clk(CLK), .Q(NextPC));  // open: clr
  Register #(.width(32)) Instruction (.D(multiplexer_2_out), .en(1'b1), .clk(CLK), .Q(Ins));  // open: clr
  Register #(.width(32)) Operand1 (.D(multiplexer_3_out), .en(1'b1), .clk(CLK), .Q(OP1out));  // open: clr
  Register #(.width(32)) Operand2 (.D(multiplexer_4_out), .en(1'b1), .clk(CLK), .Q(OP2out));  // open: clr
  Register #(.width(32)) SignExtend (.D(multiplexer_17_out), .en(1'b1), .clk(CLK), .Q(SEout));  // open: clr
  Register #(.width(5)) Destination (.D(multiplexer_5_out), .en(1'b1), .clk(CLK), .Q(RegDstOut));  // open: clr
  Register #(.width(6)) ALUOP (.D(multiplexer_6_out), .en(1'b1), .clk(CLK), .Q(ALUOPOUT));  // open: clr
  D_Flip_Flop RegDstSignal (.D(multiplexer_8_out), .clk(CLK), .Q(RegDstMUXout));  // open: Qn, preset, reset
  D_Flip_Flop Branch (.D(multiplexer_9_out), .clk(CLK), .Q(BranchOut));  // open: Qn, preset, reset
  D_Flip_Flop MemWrite (.D(multiplexer_10_out), .clk(CLK), .Q(MemWriteOut));  // open: Qn, preset, reset
  D_Flip_Flop RegWrite (.D(multiplexer_12_out), .clk(CLK), .Q(RegWriteOut));  // open: Qn, preset, reset
  D_Flip_Flop MemToReg (.D(multiplexer_13_out), .clk(CLK), .Q(MemToRegOut));  // open: Qn, preset, reset
  D_Flip_Flop ALUSrc (.D(multiplexer_7_out), .clk(CLK), .Q(ALUSrcOut));  // open: Qn, preset, reset
  D_Flip_Flop MemRead (.D(multiplexer_11_out), .clk(CLK), .Q(MemReadOut));  // open: Qn, preset, reset
  Register #(.width(5)) Rt (.D(multiplexer_14_out), .en(1'b1), .clk(CLK), .Q(rtout));  // open: clr
  Register #(.width(5)) Rs (.D(multiplexer_15_out), .en(1'b1), .clk(CLK), .Q(rsout));  // open: clr
  Register #(.width(5)) Rd (.D(multiplexer_18_out), .en(1'b1), .clk(CLK), .Q(rdout));  // open: clr
  Register #(.width(2)) register_2 (.D(multiplexer_16_out), .en(1'b1), .clk(CLK), .Q(Mode));  // open: clr

  // Notes on the sheet:
  //   EX GRUPA
  //   M Grupa
  //   W Grupa
endmodule

module EX2MEM (
  input  Flush,
  input  CLK,
  input  [31:0] NPC,
  input  [31:0] AddrIn,
  input  [31:0] ResultIn,
  input  [31:0] RegIn,
  input  ZeroIn,
  input  [4:0] RegDstIn,
  input  BranchIn,
  input  MemWriteIn,
  input  MemReadIn,
  input  [1:0] AdrMode,
  input  RegWriteIn,
  input  MemToRegIn,
  output [31:0] NextPC,
  output [31:0] AddrOut,
  output [31:0] ResultOut,
  output [31:0] RegOut,
  output ZeroOut,
  output [4:0] RegDstOut,
  output BranchOut,
  output MemWriteOut,
  output MemReadOut,
  output [1:0] Mode,
  output RegWriteOut,
  output MemToRegOut
);

  wire multiplexer_4_out, multiplexer_7_out, multiplexer_8_out, multiplexer_9_out, multiplexer_10_out,
       multiplexer_11_out;
  wire [4:0] multiplexer_5_out;
  wire [31:0] multiplexer_1_out, multiplexer_2_out, multiplexer_3_out, multiplexer_6_out;

  Multiplexer #(.width(32)) multiplexer_1 (.in0(AddrIn), .in1({32{1'b0}}), .out(multiplexer_1_out), .sel(Flush));
  Multiplexer #(.width(32)) multiplexer_2 (.in0(ResultIn), .in1({32{1'b0}}), .out(multiplexer_2_out), .sel(Flush));
  Multiplexer #(.width(32)) multiplexer_3 (.in0(RegIn), .in1({32{1'b0}}), .out(multiplexer_3_out), .sel(Flush));
  Multiplexer multiplexer_4 (.in0(ZeroIn), .in1(1'b0), .out(multiplexer_4_out), .sel(Flush));
  Multiplexer #(.width(5)) multiplexer_5 (.in0(RegDstIn), .in1({5{1'b0}}), .out(multiplexer_5_out), .sel(Flush));
  Multiplexer #(.width(32)) multiplexer_6 (.in0(NPC), .in1({32{1'b0}}), .out(multiplexer_6_out), .sel(Flush));
  Multiplexer multiplexer_7 (.in0(BranchIn), .in1(1'b0), .out(multiplexer_7_out));  // open: sel
  Multiplexer multiplexer_8 (.in0(MemWriteIn), .in1(1'b0), .out(multiplexer_8_out));  // open: sel
  Multiplexer multiplexer_9 (.in0(MemReadIn), .in1(1'b0), .out(multiplexer_9_out), .sel(Flush));
  Multiplexer multiplexer_10 (.in0(RegWriteIn), .in1(1'b0), .out(multiplexer_10_out), .sel(Flush));
  Multiplexer multiplexer_11 (.in0(MemToRegIn), .in1(1'b0), .out(multiplexer_11_out), .sel(Flush));
  Register #(.width(32)) register_1 (.D(multiplexer_6_out), .en(1'b1), .clk(CLK), .Q(NextPC));  // open: clr
  Register #(.width(32)) BranchAddr (.D(multiplexer_1_out), .en(1'b1), .clk(CLK), .Q(AddrOut));  // open: clr
  Register #(.width(32)) Result (.D(multiplexer_2_out), .en(1'b1), .clk(CLK), .Q(ResultOut));  // open: clr
  Register #(.width(32)) RegisterFileRead (.D(multiplexer_3_out), .en(1'b1), .clk(CLK), .Q(RegOut));  // open: clr
  D_Flip_Flop ZeroFlag (.D(multiplexer_4_out), .clk(CLK), .Q(ZeroOut));  // open: Qn, preset, reset
  Register #(.width(5)) Destination (.D(multiplexer_5_out), .en(1'b1), .clk(CLK), .Q(RegDstOut));  // open: clr
  D_Flip_Flop Branch (.D(multiplexer_7_out), .clk(CLK), .Q(BranchOut));  // open: Qn, preset, reset
  D_Flip_Flop MemWrite (.D(multiplexer_8_out), .clk(CLK), .Q(MemWriteOut));  // open: Qn, preset, reset
  D_Flip_Flop MemRead (.D(multiplexer_9_out), .clk(CLK), .Q(MemReadOut));  // open: Qn, preset, reset
  D_Flip_Flop RegWrite (.D(multiplexer_10_out), .clk(CLK), .Q(RegWriteOut));  // open: Qn, preset, reset
  D_Flip_Flop MemToReg (.D(multiplexer_11_out), .clk(CLK), .Q(MemToRegOut));  // open: Qn, preset, reset
  Register #(.width(2)) register_2 (.D(AdrMode), .en(1'b1), .clk(CLK), .Q(Mode));  // open: clr

  // Notes on the sheet:
  //   M Grupa
  //   W Grupa
endmodule

module MEM2WB (
  input  CLK,
  input  [31:0] ResultIn,
  input  [31:0] DataIn,
  input  [4:0] RegDstIn,
  input  RegWriteIn,
  input  MemToRegIn,
  output [31:0] ResultOut,
  output [31:0] DataOut,
  output [4:0] RegDstOut,
  output RegWriteOut,
  output MemToRegOut
);

  Register #(.width(32)) Result (.D(ResultIn), .en(1'b1), .clk(CLK), .Q(ResultOut));  // open: clr
  Register #(.width(32)) Data (.D(DataIn), .en(1'b1), .clk(CLK), .Q(DataOut));  // open: clr
  Register #(.width(5)) Destination (.D(RegDstIn), .en(1'b1), .clk(CLK), .Q(RegDstOut));  // open: clr
  D_Flip_Flop RegWrite (.D(RegWriteIn), .clk(CLK), .Q(RegWriteOut));  // open: Qn, preset, reset
  D_Flip_Flop MemToReg (.D(MemToRegIn), .clk(CLK), .Q(MemToRegOut));  // open: Qn, preset, reset

  // Notes on the sheet:
  //   W Grupa
endmodule

module HazardDetectionUnit (
  input  IDEXMemRead,
  input  [4:0] IFIDRegRs,
  input  [4:0] IDEXRegRt,
  input  [4:0] IFIDRegRt,
  output stall,
  output IFIDWrite
);

  wire comparator5b_1_eq, comparator5b_2_eq, or_1_out;

  Comparator5b comparator5b_1 (.A(IFIDRegRs), .B(IDEXRegRt), .EQ(comparator5b_1_eq));
  Comparator5b comparator5b_2 (.A(IDEXRegRt), .B(IFIDRegRt), .EQ(comparator5b_2_eq));
  and and_1 (stall, IDEXMemRead, or_1_out);
  or or_1 (or_1_out, comparator5b_1_eq, comparator5b_2_eq);
endmodule

module Comparator5b (
  input  [4:0] A,
  input  [4:0] B,
  output EQ
);

  wire xor_1_out, xor_2_out, xor_3_out, xor_4_out, xor_5_out;

  xor xor_1 (xor_1_out, A[0], B[0]);
  xor xor_2 (xor_2_out, A[1], B[1]);
  xor xor_3 (xor_3_out, A[2], B[2]);
  xor xor_4 (xor_4_out, A[3], B[3]);
  xor xor_5 (xor_5_out, A[4], B[4]);
  and and_1 (EQ, ~xor_1_out, ~xor_2_out, ~xor_3_out, ~xor_4_out, ~xor_5_out);  // AND_Gate
endmodule

module RtypeInstructionSplitter (
  input  [31:0] Instruction,
  output [5:0] Opcode,
  output [4:0] Rs,
  output [4:0] Rt,
  output [4:0] Rd,
  output [4:0] shamt,
  output [5:0] func
);


  assign func = Instruction[5:0];
  assign Opcode = Instruction[31:26];
  assign Rd = Instruction[15:11];
  assign Rs = Instruction[25:21];
  assign Rt = Instruction[20:16];
  assign shamt = Instruction[10:6];
endmodule

module SignExtendByte (
  input  [7:0] a,
  output [31:0] a32
);


  assign a32 = {{25{a[7]}}, a[6:0]};
endmodule

module ForwardUnit (
  input  [4:0] EXMrd,
  input  [4:0] MWBrd,
  input  [4:0] IDEXrs,
  input  [4:0] IDEXrt,
  input  EXMregwrite,
  input  MWBregwrite,
  output [1:0] ForwardA,
  output [1:0] ForwardB
);

  wire comparator5b_1_eq, comparator5b_2_eq, comparator5b_3_eq, comparator5b_4_eq, comparator5b_5_eq,
       comparator5b_6_eq, comparator5b_7_eq, comparator5b_8_eq, not_1_out, not_2_out, not_3_out, not_4_out,
       not_5_out, not_6_out;

  Comparator5b comparator5b_1 (.A({5{1'b0}}), .B(EXMrd), .EQ(comparator5b_1_eq));
  Comparator5b comparator5b_2 (.A({5{1'b0}}), .B(MWBrd), .EQ(comparator5b_2_eq));
  Comparator5b comparator5b_3 (.A(MWBrd), .B(IDEXrs), .EQ(comparator5b_3_eq));
  not not_1 (not_1_out, comparator5b_1_eq);
  Comparator5b comparator5b_4 (.A(EXMrd), .B(IDEXrs), .EQ(comparator5b_4_eq));
  not not_2 (not_2_out, comparator5b_2_eq);
  and and_1 (ForwardA[1], not_1_out, EXMregwrite, comparator5b_4_eq);
  Comparator5b comparator5b_5 (.A({5{1'b0}}), .B(EXMrd), .EQ(comparator5b_5_eq));
  Comparator5b comparator5b_6 (.A({5{1'b0}}), .B(MWBrd), .EQ(comparator5b_6_eq));
  Comparator5b comparator5b_7 (.A(MWBrd), .B(IDEXrt), .EQ(comparator5b_7_eq));
  not not_3 (not_3_out, ForwardA[1]);
  not not_4 (not_4_out, comparator5b_5_eq);
  Comparator5b comparator5b_8 (.A(EXMrd), .B(IDEXrt), .EQ(comparator5b_8_eq));
  not not_5 (not_5_out, comparator5b_6_eq);
  and and_2 (ForwardA[0], not_3_out, not_2_out, comparator5b_3_eq, MWBregwrite);
  and and_3 (ForwardB[0], not_4_out, EXMregwrite, comparator5b_8_eq);
  not not_6 (not_6_out, ForwardB[0]);
  and and_4 (ForwardB[1], not_6_out, not_5_out, comparator5b_7_eq, MWBregwrite);
endmodule

module mips32 (
);

  wire b, b1, clock_1_out, compare32_1_eq, control_1_alusrc, control_1_memread, control_1_memtoreg,
       control_1_memwrite, control_1_regdst, control_1_regwrite, EMreW, ex2mem_1_memreadout,
       ex2mem_1_memtoregout, ex2mem_1_memwriteout, flush, iealusel, iedsel, mem2wb_1_memtoregout, MWregW,
       RCLK, t2, t3, t4, t5, t6, WCLK, zf;
  wire [1:0] control_1_adrmode, ex2mem_1_mode, ForwardA, ForwardB, mde;
  wire [4:0] EMrd, idd, ierd, IErs, IErt, ird, irs, irt, MWrd, rdd, rtypeinstructionsplitter_2_p2, t1;
  wire [5:0] control_1_aluop, o, rtypeinstructionsplitter_1_opcode, rtypeinstructionsplitter_2_p3;
  wire [10:0] f;
  wire [31:0] adder_1_out, alu_1_result, btar, data_1_readdata, ei, ex2mem_1_resultout, f01, f10, ida, idb,
       idi, idnpc, iea, ieb, ienpc, IEse, instructions_1_instruction, ise, mem2wb_1_dataout,
       mem2wb_1_resultout, multiplexer_1_out, multiplexer_3_out, multiplexer_4_out, multiplexer_5_out, PC_q,
       shifter_1_out;

  Multiplexer #(.width(32)) multiplexer_1 (.in0(adder_1_out), .in1(btar), .out(multiplexer_1_out), .sel(b));
  Register #(.width(32)) PC (.D(multiplexer_1_out), .en(flush), .clk(WCLK), .Q(PC_q));  // open: clr
  Clock clock_1 (.out(clock_1_out));
  CLKmodul clkmodul_1 (.CLK(clock_1_out), .phase0(WCLK), .phase90(RCLK));  // open: RST
  Adder #(.width(32)) adder_1 (.a(PC_q), .b(32'h4), .out(adder_1_out));  // open: cin, cout
  Instructions instructions_1 (.Read(PC_q), .Instruction(instructions_1_instruction));
  IF2ID if2id_1 (
    .PCin(adder_1_out), .InsIn(instructions_1_instruction), .en(flush), .CLK(WCLK), .NPC(idnpc), .Ins(idi));
  SignExtend signextend_1 (.Value_u16(idnpc[15:0]), .Value_u32(ise));
  Shifter #(.width(32)) shifter_1 (.in(ise), .\dist (5'b00010), .out(shifter_1_out));
  Adder #(.width(32)) adder_2 (.a(idnpc), .b(shifter_1_out), .out(btar));  // open: cin, cout
  RtypeInstructionSplitter rtypeinstructionsplitter_1 (
    .Instruction(idnpc), .Opcode(rtypeinstructionsplitter_1_opcode), .Rs(irs), .Rt(irt), .Rd(ird));  // open: shamt, func
  Multiplexer #(.width(5)) multiplexer_2 (.in0(irt), .in1(ird), .out(idd), .sel(control_1_regdst));
  HazardDetectionUnit hazarddetectionunit_1 (
    .IDEXMemRead(t4), .IFIDRegRs(irs), .IDEXRegRt(IErt), .IFIDRegRt(irt), .stall(flush));  // open: IFIDWrite
  compare32 compare32_1 (.B(ida), .A(idb), .eq(compare32_1_eq));
  Registers registers_1 (
    .CLK(RCLK), .ReadRegister1(irs), .ReadRegister2(idd), .WriteRegister(MWrd), .WriteData(f01),
    .Write(MWregW), .WCLK(WCLK), .ReadData1(ida), .ReadData2(idb));  // open: PC
  and and_1 (b, b1, compare32_1_eq);
  Control control_1 (
    .Opcode(rtypeinstructionsplitter_1_opcode), .RegDst(control_1_regdst), .Branch(b1),
    .MemRead(control_1_memread), .MemToReg(control_1_memtoreg), .MemWrite(control_1_memwrite),
    .ALUSrc(control_1_alusrc), .RegWrite(control_1_regwrite), .AdrMode(control_1_adrmode),
    .ALUop(control_1_aluop));  // open: RegToPC
  ID2EX id2ex_1 (
    .flush(flush), .CLK(WCLK), .NPC(idnpc), .InsIn(idi), .OP1in(ida), .OP2in(idb), .SEin(ise),
    .RegDstIn(idd), .ALUOPIN(control_1_aluop), .ALUSrcIN(control_1_alusrc), .RegDstMUXin(control_1_regdst),
    .BranchIn(b1), .MemWriteIn(control_1_memwrite), .MemReadIn(control_1_memread),
    .RegWriteIn(control_1_regwrite), .MemToRegIn(control_1_memtoreg), .rtin(irt), .rsin(irs), .rdin(ird),
    .AdrMode(control_1_adrmode), .NextPC(ienpc), .Ins(ei), .OP1out(iea), .OP2out(ieb), .SEout(IEse),
    .RegDstOut(t1), .ALUOPOUT(o), .ALUSrcOut(iealusel), .RegDstMUXout(iedsel), .BranchOut(t3),
    .MemWriteOut(t2), .MemReadOut(t4), .RegWriteOut(t5), .MemToRegOut(t6), .rtout(IErt), .rsout(IErs),
    .rdout(ierd), .Mode(mde));
  // RtypeInstructionSplitter rtypeinstructionsplitter_2: pin names not known; wires that end beside it: ei, rtypeinstructionsplitter_2_p2, rtypeinstructionsplitter_2_p3
  Multiplexer #(.select(2), .width(32)) multiplexer_3 (
    .in0(ieb), .in1(f01), .in2(f10), .out(multiplexer_3_out), .sel(ForwardB));  // open: in3
  Multiplexer #(.select(2), .width(32)) multiplexer_4 (
    .in0(iea), .in1(f01), .in2(f10), .out(multiplexer_4_out), .sel(ForwardA));  // open: in3
  Multiplexer #(.width(32)) multiplexer_5 (
    .in0(multiplexer_3_out), .in1(IEse), .out(multiplexer_5_out), .sel(iealusel));
  Multiplexer #(.width(5)) multiplexer_6 (.in0(IErt), .in1(ierd), .out(rdd), .sel(iedsel));
  ALUControl alucontrol_1 (
    .SHAMT(rtypeinstructionsplitter_2_p2), .ALUop(o), .Func(rtypeinstructionsplitter_2_p3), .ALUFunc(f));
  ForwardUnit forwardunit_1 (
    .EXMrd(EMrd), .MWBrd(MWrd), .IDEXrs(IErs), .IDEXrt(IErt), .EXMregwrite(EMreW), .MWBregwrite(MWregW),
    .ForwardA(ForwardA), .ForwardB(ForwardB));
  ALU alu_1 (.Operand1(multiplexer_4_out), .Operand2(multiplexer_5_out), .ALUfunc(f), .ZF(zf), .Result(alu_1_result));
  EX2MEM ex2mem_1 (
    .Flush(flush), .CLK(WCLK), .NPC(ienpc), .AddrIn(alu_1_result), .ResultIn(multiplexer_5_out), .ZeroIn(zf),
    .RegDstIn(rdd), .BranchIn(t3), .MemWriteIn(t2), .MemReadIn(t4), .AdrMode(mde), .RegWriteIn(t5),
    .MemToRegIn(t6), .AddrOut(f10), .ResultOut(ex2mem_1_resultout), .RegDstOut(EMrd),
    .MemWriteOut(ex2mem_1_memwriteout), .MemReadOut(ex2mem_1_memreadout), .Mode(ex2mem_1_mode),
    .RegWriteOut(EMreW), .MemToRegOut(ex2mem_1_memtoregout));  // open: RegIn, NextPC, RegOut, ZeroOut, BranchOut
  Data data_1 (
    .CLK(WCLK), .Address(f10), .MemWrite(ex2mem_1_memwriteout), .MemRead(ex2mem_1_memreadout),
    .WriteData(ex2mem_1_resultout), .Mode(ex2mem_1_mode), .ReadData(data_1_readdata));
  MEM2WB mem2wb_1 (
    .CLK(WCLK), .ResultIn(f10), .DataIn(data_1_readdata), .RegDstIn(EMrd), .RegWriteIn(EMreW),
    .MemToRegIn(ex2mem_1_memtoregout), .ResultOut(mem2wb_1_resultout), .DataOut(mem2wb_1_dataout),
    .RegDstOut(MWrd), .RegWriteOut(MWregW), .MemToRegOut(mem2wb_1_memtoregout));
  Multiplexer #(.width(32)) multiplexer_7 (
    .in0(mem2wb_1_resultout), .in1(mem2wb_1_dataout), .out(f01), .sel(mem2wb_1_memtoregout));

  // Other names for the same wires on the sheet: im[15:0] = idnpc[15:0]

  // Notes on the sheet:
  //   MuxB
  //   MuxA
  //   ovo je iz alu
  //   AUTOR: TARIK HASTOR
endmodule

module compare32 (
  input  [31:0] B,
  input  [31:0] A,
  output eq
);

  wire or_1_out;
  wire [31:0] xor_1_out;

  assign xor_1_out = B ^ A;  // XOR_Gate xor_1, 32 bits wide
  or or_1 (or_1_out, xor_1_out[0], xor_1_out[1], xor_1_out[2], xor_1_out[3], xor_1_out[4], xor_1_out[5], xor_1_out[6], xor_1_out[7], xor_1_out[8], xor_1_out[9], xor_1_out[10], xor_1_out[11], xor_1_out[12], xor_1_out[13], xor_1_out[14], xor_1_out[15], xor_1_out[17], xor_1_out[18], xor_1_out[19], xor_1_out[20], xor_1_out[21], xor_1_out[22], xor_1_out[23], xor_1_out[24], xor_1_out[25], xor_1_out[26], xor_1_out[27], xor_1_out[28], xor_1_out[29], xor_1_out[30], xor_1_out[31], xor_1_out[16]);
  not not_1 (eq, or_1_out);
endmodule
